# Fritzing sketch NodeMCU (ESP8266) NeoPixel Cheerlights plus mp3 (saved by Fritzing 0.9.3b)
breadboards: 1

parts:
  U1 = NodeMCU V1.0
  Part1 = 16 NeoPixel Ring [part_number=1463]
  DFRobot_DFPlayer_Mini1 = DFRobot DFPlayer Mini [part_number=DFR0299]

nets:
  N1: U1.D0, DFRobot_DFPlayer_Mini1.IO_2
  N2: U1.D1, DFRobot_DFPlayer_Mini1.ADKEY_1
  N3: U1.D4, Part1.IN
  GND: U1.GND, Part1.GND
  VIN: U1.Vin, Part1.VDD

notes:
  Project Notes:
  MP3 player pictured is used for representation only.
  MP3 player used was a Serial model Catalex
  Blue Wire D0 - connect to TX of player
  Purple Wire D1 - connect to RX of player
  NOTE: Pictured is a version 1.0 of the NodeMCU mine is a version .9 - the difference I can see is
  VIN pin is 5v on the v.9
  The neopixels and mp3 player should be connected to 5v, but may work at 3.3v

custom parts:
  NodeMCU V1.0: ESP8266 based NodeMCU
  16 NeoPixel Ring: 16 ultra bright smart LED NeoPixels are arranged in a circle with 1.75" (44.5mm) outer diameter. The rings are 'chainable' - connect the output pin of one to the input pin of another. Use only one microcontroller pin to control as many as you can chain together! Each LED is addressable as the driver chip is inside the LED. Each one has ~18mA constant current drive so the color will be very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
