# Fritzing sketch NodeMCU (ESP8266) NeoPixel Cheerlights (saved by Fritzing 0.9.3b)
breadboards: 1

parts:
  U1 = NodeMCU V1.0
  Part1 = 16 NeoPixel Ring [part_number=1463]

nets:
  N1: U1.D4, Part1.IN
  GND: U1.GND, Part1.GND
  VIN: U1.Vin, Part1.VDD

custom parts:
  NodeMCU V1.0: ESP8266 based NodeMCU
  16 NeoPixel Ring: 16 ultra bright smart LED NeoPixels are arranged in a circle with 1.75" (44.5mm) outer diameter. The rings are 'chainable' - connect the output pin of one to the input pin of another. Use only one microcontroller pin to control as many as you can chain together! Each LED is addressable as the driver chip is inside the LED. Each one has ~18mA constant current drive so the color will be very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
